// Digital circuit lcd.dig as structural Verilog
module lcd (
  input  clk
);

  wire and_1_out, comparator_1_lt, not_1_out;
  wire [2:0] sub_1_s;
  wire [4:0] barrelshifter_1_out, CGROM_d;
  wire [7:0] div_3_q;
  wire [10:0] DDRAM_d;
  wire [12:0] counter_1_out, div_1_q, div_1_r, div_3_r;
  wire [12:2] div_2_q;
  wire [12:3] div_2_r;
  wire [12:6] div_3_q_2;

  Counter #(.Bits(13)) counter_1 (.en(1'b1), .C(clk), .clr(1'b0), .out(counter_1_out));  // open: ovf
  ROM #(.AddrBits(8), .Bits(8)) DDRAM (.A(div_3_q), .sel(1'b1), .D(DDRAM_d[10:3]));
  Comparator #(.Bits(13)) comparator_1 (.a(counter_1_out), .b(13'hc80), .lt(comparator_1_lt));  // open: gt, eq
  // Probe P_i on counter_1_out
  Div #(.Bits(13)) div_1 (.a(counter_1_out), .b(13'h64), .q(div_1_q), .r(div_1_r));
  and and_1 (and_1_out, comparator_1_lt, clk);
  // Probe on DDRAM_d
  ROM #(.AddrBits(11), .Bits(5)) CGROM (.A(DDRAM_d), .sel(1'b1), .D(CGROM_d));
  // Probe P_R on div_1_q
  // Probe P_C on div_1_r
  Div #(.Bits(13)) div_2 (.a(div_1_q), .b(13'h8), .q({div_2_q, div_3_q[7:6]}), .r({div_2_r, DDRAM_d[2:0]}));
  Div #(.Bits(13)) div_3 (.a(div_1_r), .b(13'h5), .q({div_3_q_2, div_3_q[5:0]}), .r(div_3_r));
  Sub #(.Bits(3)) sub_1 (.a(3'b100), .b(div_3_r[2:0]), .c_i(1'b0), .s(sub_1_s));  // open: c_o
  BarrelShifter #(.Bits(5), .barrelShifterMode("rotate"), .direction("right")) barrelshifter_1 (
    .in(CGROM_d), .shift(sub_1_s), .out(barrelshifter_1_out));
  // Probe C_R on {div_2_q, div_3_q[7:6]}
  // Probe C_C on {div_3_q_2, div_3_q[5:0]}
  // Probe D_R on DDRAM_d[2:0]
  // Probe D_C on div_3_r[2:0]
  not not_1 (not_1_out, and_1_out);
  GraphicCard #(.graphicHeight(32), .graphicWidth(100)) graphiccard_1 (
    .A(counter_1_out), .str(1'b1), .C(not_1_out), .ld(1'b0), .B(1'b0), .D(barrelshifter_1_out[0]));

  // Notes on the sheet:
  //   clk: Hz: 50
  //   contents of DDRAM (hex, n*v repeats v):
  //   30,31,30,31,31,31,59*0,31,64*0,31,64*0,31
  //   contents of CGROM (hex, n*v repeats v):
  //   49*0,e040404040c04,1f08040201110e,333*0,e,11,13,15,19,11,e,0,4
  //   ,c,4*4,e
endmodule
