// Digital circuit lutcomp.dig as structural Verilog
module lutcomp (
  input  RESET,
  input  clk
);

  wire CLK_t, CLK_t_t, HALT, not_2_out, not_3_out, switch_1_b, uc_1_p4, uc_1_p5, uc_1_p6, uc_1_p7, uc_1_p8,
       uc_1_p9, uc_1_p10, uc_1_p11, uc_1_p12, uc_1_p13, uc_1_p14, uc_1_p15, uc_1_p16, uc_1_p17, uc_1_p18,
       uc_1_p20, uc_1_p21, uc_1_p22, uc_1_p23, undriven, undriven_2, undriven_3, undriven_4, undriven_8,
       undriven_9, undriven_10, undriven_11, undriven_12;
  wire [3:0] undriven_7;
  wire [6:0] keyboard_1_d, uc_1_p3, undriven_5;
  wire [7:0] notconnected_1_out, notconnected_2_out, notconnected_3_out, notconnected_4_out, undriven_6;
  wire [7:7] keyboard_1_av, uc_1_p3_2;
  wire [15:7] keyboard_1_d_2;
  wire [23:0] pc_1_addr, pc_1_pc;

  and and_1 (CLK_t, clk, HALT);
  Stop stop_1 (.stop(~HALT));
  not not_1 (CLK_t_t, CLK_t);
  // uc uc_1: pin names not known; wires that end beside it: CLK_t_t, RESET, {uc_1_p3_2[7], uc_1_p3}, uc_1_p4, uc_1_p5, uc_1_p6, uc_1_p7, uc_1_p8, uc_1_p9, uc_1_p10, uc_1_p11, uc_1_p12, uc_1_p13, uc_1_p14, uc_1_p15, uc_1_p16, uc_1_p17, uc_1_p18, HALT, uc_1_p20, uc_1_p21, uc_1_p22, uc_1_p23
  not not_2 (not_2_out, uc_1_p4);
  // Probe on undriven_8
  // Probe on undriven_9
  // Probe on undriven_10
  // Probe on undriven_11
  // Probe on undriven_12
  Switch switch_1 (.A(uc_1_p6), .B(switch_1_b));
  pc pc_1 (
    .PC_INC(uc_1_p6), .RESET(RESET), .PC_SPE(uc_1_p23), .OE(not_2_out), .ADDR(pc_1_addr), .PC(pc_1_pc));  // open: ADDR_IN
  // Probe $uPC on {undriven_7, undriven_6, undriven_5}
  // Probe on undriven_5
  // Probe $IR0 on undriven_6
  // Probe $FLAGS on undriven_7
  Break break_1 (.brk(switch_1_b));
  PullDown pulldown_1 (.out(switch_1_b));
  // Probe PC on pc_1_pc
  not not_3 (not_3_out, uc_1_p22);
  Keyboard keyboard_1 (.C(uc_1_p10), .en(1'b1), .D({keyboard_1_d_2, keyboard_1_d}), .av(keyboard_1_av[7]));
  // Probe on {1'b0, uc_1_p3}
  Terminal terminal_1 (.D({1'b0, uc_1_p3}), .C(uc_1_p18), .en(1'b1));
  Break break_2 (.brk(not_3_out));
  memory memory_1 (
    .MEM_CP(uc_1_p9), .ADDR_OE(uc_1_p4), .A0_CP(uc_1_p15), .A1_CP(uc_1_p16), .A2_CP(uc_1_p17),
    .MEM_OE(uc_1_p21), .DATA({uc_1_p3_2[7], uc_1_p3}), .ADDR(pc_1_addr));  // open: DATA_2, ADDR_2
  \reg  W (.OE(undriven), .CP(uc_1_p11), .DATA(notconnected_1_out), .IO({uc_1_p3_2[7], uc_1_p3}));
  // NotConnected on notconnected_1_out
  \reg  X (.OE(undriven_2), .CP(uc_1_p12), .DATA(notconnected_2_out), .IO({uc_1_p3_2[7], uc_1_p3}));
  // NotConnected on notconnected_2_out
  \reg  Y (.OE(undriven_3), .CP(uc_1_p13), .DATA(notconnected_3_out), .IO({uc_1_p3_2[7], uc_1_p3}));
  // NotConnected on notconnected_3_out
  \reg  Z (.OE(undriven_4), .CP(uc_1_p14), .DATA(notconnected_4_out), .IO({uc_1_p3_2[7], uc_1_p3}));
  // NotConnected on notconnected_4_out
  assign {uc_1_p3_2[7], uc_1_p3} = ~uc_1_p22 ? {keyboard_1_av[7], keyboard_1_d} : 8'bz;  // DriverInvSel driverinvsel_1
  // Probe ADDR on pc_1_addr
  // Probe DATA on {uc_1_p3_2[7], uc_1_p3}
  // alu alu_1: pin names not known; wires that end beside it: uc_1_p5, uc_1_p20, uc_1_p8, uc_1_p7, {uc_1_p3_2[7], uc_1_p3}

  // Notes on the sheet:
  //   RESET: default 1
  //   clk: Hz: 10000
  //   4A
  //   4B
  //   4Y
  //   6A
  //   6Y
  //   3A
  //   3Y
endmodule
